// Logisim project main.circ as structural Verilog: 18 circuits, main circuit am08x24arc-main
module am08x24arc_main (
  input  in_1
);

  wire and_1_out, and_2_out, and_3_out, and_4_out, and_5_out, and_6_out, and_7_out, and_8_out, BADOP, CLOCK,
       comparator_1_eq, counter_1_carry, DEVICE_ENABLE, DEVICE_SELECT, DEVICE_SRC, GPU_CLOCK,
       GPU_DEVICE_ENABLE, GPU_DEVICE_SELECT, GPU_DEVICE_SRC, INC_PC, n8x_device_selector_1_out_4,
       n8x_device_selector_1_out_5, n8x_device_selector_1_out_11, n16x_device_selector_1_out_4,
       n16x_device_selector_1_out_5, n16x_device_selector_1_out_6, not_1_out, not_2_out, undriven;
  wire [15:0] ADRESS_BUS, DATA_BUS, GPU_ADRESS_BUS, GPU_DATA_BUS, Instruction_ROM_2_data,
       n16bit_2thread_register_1_stored, PC, register_1_q, register_2_q, register_3_q;
  wire [23:0] INSTRUCTION;
  wire [31:0] n2x32x32bit_combiner_1_out_65, n2x32x32bit_combiner_1_out_66, n2x32x32bit_combiner_1_out_67,
       n2x32x32bit_combiner_1_out_68, n2x32x32bit_combiner_1_out_69, n2x32x32bit_combiner_1_out_70,
       n2x32x32bit_combiner_1_out_71, n2x32x32bit_combiner_1_out_72, n2x32x32bit_combiner_1_out_73,
       n2x32x32bit_combiner_1_out_74, n2x32x32bit_combiner_1_out_75, n2x32x32bit_combiner_1_out_76,
       n2x32x32bit_combiner_1_out_77, n2x32x32bit_combiner_1_out_78, n2x32x32bit_combiner_1_out_79,
       n2x32x32bit_combiner_1_out_80, n2x32x32bit_combiner_1_out_81, n2x32x32bit_combiner_1_out_82,
       n2x32x32bit_combiner_1_out_83, n2x32x32bit_combiner_1_out_84, n2x32x32bit_combiner_1_out_85,
       n2x32x32bit_combiner_1_out_86, n2x32x32bit_combiner_1_out_87, n2x32x32bit_combiner_1_out_88,
       n2x32x32bit_combiner_1_out_89, n2x32x32bit_combiner_1_out_90, n2x32x32bit_combiner_1_out_91,
       n2x32x32bit_combiner_1_out_92, n2x32x32bit_combiner_1_out_93, n2x32x32bit_combiner_1_out_94,
       n2x32x32bit_combiner_1_out_95, n2x32x32bit_combiner_1_out_96, n32x32bit_screen_buffer_1_out_6,
       n32x32bit_screen_buffer_1_out_7, n32x32bit_screen_buffer_1_out_8, n32x32bit_screen_buffer_1_out_9,
       n32x32bit_screen_buffer_1_out_10, n32x32bit_screen_buffer_1_out_11, n32x32bit_screen_buffer_1_out_12,
       n32x32bit_screen_buffer_1_out_13, n32x32bit_screen_buffer_1_out_14, n32x32bit_screen_buffer_1_out_15,
       n32x32bit_screen_buffer_1_out_16, n32x32bit_screen_buffer_1_out_17, n32x32bit_screen_buffer_1_out_18,
       n32x32bit_screen_buffer_1_out_19, n32x32bit_screen_buffer_1_out_20, n32x32bit_screen_buffer_1_out_21,
       n32x32bit_screen_buffer_1_out_23, n32x32bit_screen_buffer_1_out_24, n32x32bit_screen_buffer_1_out_25,
       n32x32bit_screen_buffer_1_out_26, n32x32bit_screen_buffer_1_out_28, n32x32bit_screen_buffer_1_out_29,
       n32x32bit_screen_buffer_1_out_30, n32x32bit_screen_buffer_1_out_31, n32x32bit_screen_buffer_1_out_32,
       n32x32bit_screen_buffer_1_out_33, n32x32bit_screen_buffer_1_out_34, n32x32bit_screen_buffer_1_out_35,
       n32x32bit_screen_buffer_1_out_36, n32x32bit_screen_buffer_1_out_37, n32x32bit_screen_buffer_2_out_6,
       n32x32bit_screen_buffer_2_out_7, n32x32bit_screen_buffer_2_out_9, n32x32bit_screen_buffer_2_out_10,
       n32x32bit_screen_buffer_2_out_11, n32x32bit_screen_buffer_2_out_12, n32x32bit_screen_buffer_2_out_13,
       n32x32bit_screen_buffer_2_out_14, n32x32bit_screen_buffer_2_out_15, n32x32bit_screen_buffer_2_out_16,
       n32x32bit_screen_buffer_2_out_17, n32x32bit_screen_buffer_2_out_18, n32x32bit_screen_buffer_2_out_19,
       n32x32bit_screen_buffer_2_out_20, n32x32bit_screen_buffer_2_out_21, n32x32bit_screen_buffer_2_out_22,
       n32x32bit_screen_buffer_2_out_23, n32x32bit_screen_buffer_2_out_24, n32x32bit_screen_buffer_2_out_25,
       n32x32bit_screen_buffer_2_out_26, n32x32bit_screen_buffer_2_out_27, n32x32bit_screen_buffer_2_out_28,
       n32x32bit_screen_buffer_2_out_29, n32x32bit_screen_buffer_2_out_30, n32x32bit_screen_buffer_2_out_31,
       n32x32bit_screen_buffer_2_out_32, n32x32bit_screen_buffer_2_out_33, n32x32bit_screen_buffer_2_out_34,
       n32x32bit_screen_buffer_2_out_35, n32x32bit_screen_buffer_2_out_36, n32x32bit_screen_buffer_2_out_37;

  am08x24arc_cpu am08x24arc_cpu_1 (
    .DATA_BUS_OUT(DATA_BUS), .ADRESS_BUS(ADRESS_BUS), .CLOCK(CLOCK), .INC_PC(INC_PC), .HALT(BADOP),
    .BADOP(BADOP), .DEVICE_SRC(DEVICE_SRC), .SELECT_DEVICE(DEVICE_SELECT), .DEVICE_ENABLE(DEVICE_ENABLE),
    .DATA_BUS_IN(DATA_BUS), .PC(PC), .INSTRUCTION(INSTRUCTION));
  am08x24arc_clock am08x24arc_clock_1 (.HALT(BADOP), .BADOP(BADOP), .CLOCK(CLOCK), .INC_PC(INC_PC));
  _16x_device_selector u_16x_device_selector_1 (
    .DEVICE(DATA_BUS), .DEVICE_SELECT(DEVICE_SELECT), .CLOCK(CLOCK), .out_4(n16x_device_selector_1_out_4),
    .out_5(n16x_device_selector_1_out_5), .out_6(n16x_device_selector_1_out_6));  // open: out_7, out_8, out_9, out_10, out_11, out_12, out_13, out_14, out_15, out_16, out_17, out_18, out_19
  Comparator #(.width(16)) comparator_1 (.a(ADRESS_BUS), .b({16{1'b0}}), .eq(comparator_1_eq));  // open: gt, lt
  and and_1 (and_1_out, n16x_device_selector_1_out_6, comparator_1_eq, DEVICE_ENABLE);
  // Probe on n16bit_2thread_register_1_stored
  and and_2 (and_2_out, ~comparator_1_eq, n16x_device_selector_1_out_6, DEVICE_ENABLE);  // AND_Gate
  LED led_1 (.in(undriven));
  not not_1 (not_1_out, DEVICE_ENABLE);
  not not_2 (not_2_out, and_3_out);
  and and_3 (and_3_out, n16x_device_selector_1_out_5, DEVICE_ENABLE);
  and and_4 (and_4_out, n8x_device_selector_1_out_4, GPU_DEVICE_ENABLE);
  _16bit_2thread_register u_16bit_2thread_register_1 (
    .CLOCK_0(CLOCK), .ENABLE_0(and_1_out), .DEVICE_SRC_0(DEVICE_SRC), .DATA_BUS_0_IN(DATA_BUS),
    .DATA_BUS_0_OUT(DATA_BUS), .CLOCK_1(GPU_CLOCK), .ENABLE_1(and_4_out), .DEVICE_SRC_1(GPU_DEVICE_SRC),
    .DATA_BUS_1_IN(GPU_DATA_BUS), .DATA_BUS_1_OUT(GPU_DATA_BUS), .STORED(n16bit_2thread_register_1_stored));  // open: SEL
  and and_5 (and_5_out, n8x_device_selector_1_out_5, GPU_DEVICE_ENABLE);
  _16bit_2semi_thread_ram u_16bit_2semi_thread_ram_1 (
    .CLOCK_0(CLOCK), .ENABLE_0(and_2_out), .DEVICE_SRC_0(DEVICE_SRC), .DATA_BUS_0_IN(DATA_BUS),
    .DATA_BUS_0_OUT(DATA_BUS), .ADRESS_0(ADRESS_BUS), .CLOCK_1(GPU_CLOCK), .ENABLE_1(and_5_out),
    .DEVICE_SRC_1(GPU_DEVICE_SRC), .DATA_BUS_1_IN(GPU_DATA_BUS), .DATA_BUS_1_OUT(GPU_DATA_BUS),
    .ADRESS_1(GPU_ADRESS_BUS), .WRONG_INPUT(undriven));
  ROM #(.addrWidth(16), .dataWidth(24), .Select("low")) Instruction_ROM (.addr(PC), .data(INSTRUCTION));
  // Probe on DATA_BUS
  assign DATA_BUS = and_6_out ? Instruction_ROM_2_data : 16'bz;  // Controlled_Buffer controlled_buffer_1
  ROM #(.addrWidth(16), .dataWidth(16), .Select("low")) Instruction_ROM_2 (
    .addr(ADRESS_BUS), .data(Instruction_ROM_2_data), .sel(not_1_out));
  and and_6 (and_6_out, DEVICE_ENABLE, DEVICE_SRC, n16x_device_selector_1_out_4);
  RAM #(.addrWidth(16), .dataWidth(16), .Select("low")) ram_1 (
    .addr(ADRESS_BUS), .data(DATA_BUS), .sel(not_2_out), .clk(CLOCK), .ld(DEVICE_SRC));  // open: clr
  _8x_device_selector u_8x_device_selector_1 (
    .DEVICE(GPU_DATA_BUS), .DEVICE_SELECT(GPU_DEVICE_SELECT), .CLOCK(GPU_CLOCK),
    .out_4(n8x_device_selector_1_out_4), .out_5(n8x_device_selector_1_out_5),
    .out_11(n8x_device_selector_1_out_11));  // open: out_6, out_7, out_8, out_9, out_10
  and and_7 (and_7_out, n8x_device_selector_1_out_11, GPU_DEVICE_ENABLE, GPU_CLOCK);
  am08x24arc_gpu_main_core am08x24arc_gpu_main_core_1 (
    .CLOCK(GPU_CLOCK), .out_3(GPU_ADRESS_BUS), .out_2(GPU_DATA_BUS), .DEVICE_SELECT(GPU_DEVICE_SELECT),
    .DEVICE_SRC(GPU_DEVICE_SRC), .DEVICE_ENABLE(GPU_DEVICE_ENABLE), .in_1(GPU_DATA_BUS));
  and and_8 (and_8_out, and_7_out, ~counter_1_carry);  // AND_Gate
  Register #(.width(16), .Select("low")) register_1 (
    .D(register_2_q), .Q(register_1_q), .clk(and_8_out));  // open: en, clr
  Register #(.width(16), .Select("low")) register_2 (
    .D(GPU_DATA_BUS), .Q(register_2_q), .clk(and_8_out));  // open: en, clr
  Register #(.width(16), .Select("low")) register_3 (
    .D(register_1_q), .Q(register_3_q), .clk(and_8_out));  // open: en, clr
  Counter #(.max('h3), .trigger("falling")) counter_1 (
    .carry(counter_1_carry), .clk(and_7_out));  // open: load, D, count, Q, clr, preset, down
  _32x32bit_screen_buffer u_32x32bit_screen_buffer_1 (
    .DATA_IN({register_2_q, register_1_q}), .ADRESS(register_3_q), .BLOCK(1'b1), .CLOCK(counter_1_carry),
    .out_6(n32x32bit_screen_buffer_1_out_6), .out_7(n32x32bit_screen_buffer_1_out_7),
    .out_8(n32x32bit_screen_buffer_1_out_8), .out_9(n32x32bit_screen_buffer_1_out_9),
    .out_10(n32x32bit_screen_buffer_1_out_10), .out_11(n32x32bit_screen_buffer_1_out_11),
    .out_12(n32x32bit_screen_buffer_1_out_12), .out_13(n32x32bit_screen_buffer_1_out_13),
    .out_14(n32x32bit_screen_buffer_1_out_14), .out_15(n32x32bit_screen_buffer_1_out_15),
    .out_16(n32x32bit_screen_buffer_1_out_16), .out_17(n32x32bit_screen_buffer_1_out_17),
    .out_18(n32x32bit_screen_buffer_1_out_18), .out_19(n32x32bit_screen_buffer_1_out_19),
    .out_20(n32x32bit_screen_buffer_1_out_20), .out_21(n32x32bit_screen_buffer_1_out_21), .SEL(in_1),
    .out_23(n32x32bit_screen_buffer_1_out_23), .out_24(n32x32bit_screen_buffer_1_out_24),
    .out_25(n32x32bit_screen_buffer_1_out_25), .out_26(n32x32bit_screen_buffer_1_out_26),
    .out_28(n32x32bit_screen_buffer_1_out_28), .out_29(n32x32bit_screen_buffer_1_out_29),
    .out_30(n32x32bit_screen_buffer_1_out_30), .out_31(n32x32bit_screen_buffer_1_out_31),
    .out_32(n32x32bit_screen_buffer_1_out_32), .out_33(n32x32bit_screen_buffer_1_out_33),
    .out_34(n32x32bit_screen_buffer_1_out_34), .out_35(n32x32bit_screen_buffer_1_out_35),
    .out_36(n32x32bit_screen_buffer_1_out_36), .out_37(n32x32bit_screen_buffer_1_out_37));  // open: out_22, out_27
  _32x32bit_screen_buffer u_32x32bit_screen_buffer_2 (
    .DATA_IN({register_2_q, register_1_q}), .ADRESS(register_3_q), .BLOCK(1'b1), .CLOCK(counter_1_carry),
    .out_6(n32x32bit_screen_buffer_2_out_6), .out_7(n32x32bit_screen_buffer_2_out_7),
    .out_9(n32x32bit_screen_buffer_2_out_9), .out_10(n32x32bit_screen_buffer_2_out_10),
    .out_11(n32x32bit_screen_buffer_2_out_11), .out_12(n32x32bit_screen_buffer_2_out_12),
    .out_13(n32x32bit_screen_buffer_2_out_13), .out_14(n32x32bit_screen_buffer_2_out_14),
    .out_15(n32x32bit_screen_buffer_2_out_15), .out_16(n32x32bit_screen_buffer_2_out_16),
    .out_17(n32x32bit_screen_buffer_2_out_17), .out_18(n32x32bit_screen_buffer_2_out_18),
    .out_19(n32x32bit_screen_buffer_2_out_19), .out_20(n32x32bit_screen_buffer_2_out_20),
    .out_21(n32x32bit_screen_buffer_2_out_21), .SEL(in_1), .out_22(n32x32bit_screen_buffer_2_out_22),
    .out_23(n32x32bit_screen_buffer_2_out_23), .out_24(n32x32bit_screen_buffer_2_out_24),
    .out_25(n32x32bit_screen_buffer_2_out_25), .out_26(n32x32bit_screen_buffer_2_out_26),
    .out_27(n32x32bit_screen_buffer_2_out_27), .out_28(n32x32bit_screen_buffer_2_out_28),
    .out_29(n32x32bit_screen_buffer_2_out_29), .out_30(n32x32bit_screen_buffer_2_out_30),
    .out_31(n32x32bit_screen_buffer_2_out_31), .out_32(n32x32bit_screen_buffer_2_out_32),
    .out_33(n32x32bit_screen_buffer_2_out_33), .out_34(n32x32bit_screen_buffer_2_out_34),
    .out_35(n32x32bit_screen_buffer_2_out_35), .out_36(n32x32bit_screen_buffer_2_out_36),
    .out_37(n32x32bit_screen_buffer_2_out_37));  // open: out_8
  _2x32x32bit_combiner u_2x32x32bit_combiner_1 (
    .in_1(n32x32bit_screen_buffer_1_out_6), .in_2(n32x32bit_screen_buffer_1_out_7),
    .in_3(n32x32bit_screen_buffer_1_out_8), .in_4(n32x32bit_screen_buffer_1_out_9),
    .in_5(n32x32bit_screen_buffer_1_out_10), .in_6(n32x32bit_screen_buffer_1_out_11),
    .in_7(n32x32bit_screen_buffer_1_out_12), .in_8(n32x32bit_screen_buffer_1_out_13),
    .in_9(n32x32bit_screen_buffer_1_out_14), .in_10(n32x32bit_screen_buffer_1_out_15),
    .in_11(n32x32bit_screen_buffer_1_out_16), .in_12(n32x32bit_screen_buffer_1_out_17),
    .in_13(n32x32bit_screen_buffer_1_out_18), .in_14(n32x32bit_screen_buffer_1_out_19),
    .in_15(n32x32bit_screen_buffer_1_out_20), .in_16(n32x32bit_screen_buffer_1_out_21),
    .in_18(n32x32bit_screen_buffer_1_out_23), .in_19(n32x32bit_screen_buffer_1_out_24),
    .in_20(n32x32bit_screen_buffer_1_out_25), .in_21(n32x32bit_screen_buffer_1_out_26),
    .in_23(n32x32bit_screen_buffer_1_out_28), .in_24(n32x32bit_screen_buffer_1_out_29),
    .in_25(n32x32bit_screen_buffer_1_out_30), .in_26(n32x32bit_screen_buffer_1_out_31),
    .in_27(n32x32bit_screen_buffer_1_out_32), .in_28(n32x32bit_screen_buffer_1_out_33),
    .in_29(n32x32bit_screen_buffer_1_out_34), .in_30(n32x32bit_screen_buffer_1_out_35),
    .in_31(n32x32bit_screen_buffer_1_out_36), .in_32(n32x32bit_screen_buffer_1_out_37),
    .in_33(n32x32bit_screen_buffer_2_out_6), .in_34(n32x32bit_screen_buffer_2_out_7),
    .in_36(n32x32bit_screen_buffer_2_out_9), .in_37(n32x32bit_screen_buffer_2_out_10),
    .in_38(n32x32bit_screen_buffer_2_out_11), .in_39(n32x32bit_screen_buffer_2_out_12),
    .in_40(n32x32bit_screen_buffer_2_out_13), .in_41(n32x32bit_screen_buffer_2_out_14),
    .in_42(n32x32bit_screen_buffer_2_out_15), .in_43(n32x32bit_screen_buffer_2_out_16),
    .in_44(n32x32bit_screen_buffer_2_out_17), .in_45(n32x32bit_screen_buffer_2_out_18),
    .in_46(n32x32bit_screen_buffer_2_out_19), .in_47(n32x32bit_screen_buffer_2_out_20),
    .in_48(n32x32bit_screen_buffer_2_out_21), .in_49(n32x32bit_screen_buffer_2_out_22),
    .in_50(n32x32bit_screen_buffer_2_out_23), .in_51(n32x32bit_screen_buffer_2_out_24),
    .in_52(n32x32bit_screen_buffer_2_out_25), .in_53(n32x32bit_screen_buffer_2_out_26),
    .in_54(n32x32bit_screen_buffer_2_out_27), .in_55(n32x32bit_screen_buffer_2_out_28),
    .in_56(n32x32bit_screen_buffer_2_out_29), .in_57(n32x32bit_screen_buffer_2_out_30),
    .in_58(n32x32bit_screen_buffer_2_out_31), .in_59(n32x32bit_screen_buffer_2_out_32),
    .in_60(n32x32bit_screen_buffer_2_out_33), .in_61(n32x32bit_screen_buffer_2_out_34),
    .in_62(n32x32bit_screen_buffer_2_out_35), .in_63(n32x32bit_screen_buffer_2_out_36),
    .in_64(n32x32bit_screen_buffer_2_out_37), .out_65(n2x32x32bit_combiner_1_out_65),
    .out_66(n2x32x32bit_combiner_1_out_66), .out_67(n2x32x32bit_combiner_1_out_67),
    .out_68(n2x32x32bit_combiner_1_out_68), .out_69(n2x32x32bit_combiner_1_out_69),
    .out_70(n2x32x32bit_combiner_1_out_70), .out_71(n2x32x32bit_combiner_1_out_71),
    .out_72(n2x32x32bit_combiner_1_out_72), .out_73(n2x32x32bit_combiner_1_out_73),
    .out_74(n2x32x32bit_combiner_1_out_74), .out_75(n2x32x32bit_combiner_1_out_75),
    .out_76(n2x32x32bit_combiner_1_out_76), .out_77(n2x32x32bit_combiner_1_out_77),
    .out_78(n2x32x32bit_combiner_1_out_78), .out_79(n2x32x32bit_combiner_1_out_79),
    .out_80(n2x32x32bit_combiner_1_out_80), .out_81(n2x32x32bit_combiner_1_out_81),
    .out_82(n2x32x32bit_combiner_1_out_82), .out_83(n2x32x32bit_combiner_1_out_83),
    .out_84(n2x32x32bit_combiner_1_out_84), .out_85(n2x32x32bit_combiner_1_out_85),
    .out_86(n2x32x32bit_combiner_1_out_86), .out_87(n2x32x32bit_combiner_1_out_87),
    .out_88(n2x32x32bit_combiner_1_out_88), .out_89(n2x32x32bit_combiner_1_out_89),
    .out_90(n2x32x32bit_combiner_1_out_90), .out_91(n2x32x32bit_combiner_1_out_91),
    .out_92(n2x32x32bit_combiner_1_out_92), .out_93(n2x32x32bit_combiner_1_out_93),
    .out_94(n2x32x32bit_combiner_1_out_94), .out_95(n2x32x32bit_combiner_1_out_95),
    .out_96(n2x32x32bit_combiner_1_out_96));  // open: in_17, in_22, in_35
  DotMatrix #(.inputtype("row"), .matrixcols(32), .matrixrows(32)) dotmatrix_1 (
    .row0(n2x32x32bit_combiner_1_out_65), .row1(n2x32x32bit_combiner_1_out_66),
    .row2(n2x32x32bit_combiner_1_out_67), .row3(n2x32x32bit_combiner_1_out_68),
    .row4(n2x32x32bit_combiner_1_out_69), .row5(n2x32x32bit_combiner_1_out_70),
    .row6(n2x32x32bit_combiner_1_out_71), .row7(n2x32x32bit_combiner_1_out_72),
    .row8(n2x32x32bit_combiner_1_out_73), .row9(n2x32x32bit_combiner_1_out_74),
    .row10(n2x32x32bit_combiner_1_out_75), .row11(n2x32x32bit_combiner_1_out_76),
    .row12(n2x32x32bit_combiner_1_out_77), .row13(n2x32x32bit_combiner_1_out_78),
    .row14(n2x32x32bit_combiner_1_out_79), .row15(n2x32x32bit_combiner_1_out_80),
    .row16(n2x32x32bit_combiner_1_out_81), .row17(n2x32x32bit_combiner_1_out_82),
    .row18(n2x32x32bit_combiner_1_out_83), .row19(n2x32x32bit_combiner_1_out_84),
    .row20(n2x32x32bit_combiner_1_out_85), .row21(n2x32x32bit_combiner_1_out_86),
    .row22(n2x32x32bit_combiner_1_out_87), .row23(n2x32x32bit_combiner_1_out_88),
    .row24(n2x32x32bit_combiner_1_out_89), .row25(n2x32x32bit_combiner_1_out_90),
    .row26(n2x32x32bit_combiner_1_out_91), .row27(n2x32x32bit_combiner_1_out_92),
    .row28(n2x32x32bit_combiner_1_out_93), .row29(n2x32x32bit_combiner_1_out_94),
    .row30(n2x32x32bit_combiner_1_out_95), .row31(n2x32x32bit_combiner_1_out_96));

  // Other names for the same wires on the sheet: HALT = BADOP

  // Notes on the sheet:
  //   am08x24arc-main
  //   contents of Instruction_ROM (hex, n*v repeats v):
  //   17000e b0000 1b0005 30000 170001 30000 30000 10003 c0000 60000 30000 60000 30000 180000 10000 10000
  //   50000 50000 240000 a0000 60000 10001 c0000 60000 30000 60000 30000 a0000 60000 30000 240002 20000
  //   10001 170001 30000 10005 80000 30000 20000 10004 170001 30000 80001 30000 80002 30000 80003 30000
  //   10003 80000 30000 10002 c0000 60000 30000 60000 30000 60000 10001 c0000 60000 30000 60000 30000
  //   60000 170010
  //   contents of Instruction_ROM_2 (hex, n*v repeats v):
  //   8*ffff 4003 fff8 f fff8 f fff8 1f fff8 1f fff8 f fffc f fffc 2003 fff8 6003 fff0 6003 fff0 4003 fff0
  //   4003 fff8 8003 ffff 8003 ffff 8003 ffff 7 ffff 7 fffe 7 fffe 7 fffe f ffff 800f ffff c00f ffff f01f
  //   ffff f07f 9*ffff
  //   gpu-state
  //   gpu-data
  //   am08x24-gpu
endmodule

module am08x24arc_cpu (
  input  CLOCK,
  input  INC_PC,
  input  [15:0] DATA_BUS_IN,
  input  [23:0] INSTRUCTION,
  output [15:0] DATA_BUS_OUT,
  output HALT,
  output BADOP,
  output [15:0] ADRESS_BUS,
  output [15:0] PC,
  output SELECT_DEVICE,
  output DEVICE_SRC,
  output DEVICE_ENABLE
);

  wire ALU_ADRESS_SRC, ALU_SRC, and_1_out, and_2_out, and_3_out, comparator_1_eq, comparator_1_gt,
       comparator_1_lt, JNEG, JPOS, JZ, OPERAND_ADRESS_SRC, OPERAND_SRC, or_1_out, or_2_out, PC_ADRESS_SRC,
       PC_SRC, PC_t, STACK_NEXT_ADRES_SRC, STACK_NEXT_SRC, STACK_TOP_ADRESS_SRC, STACK_TOP_SRC;
  wire [1:0] ALU_ARG, STACK_OP, STACK_OP_EXTRA;
  wire [2:0] ADRESS_SRC, DATA_BUS_SRC, SRC;
  wire [3:0] ALU_OP;
  wire [15:0] ALU_OUT, DATA_BUS, STACK_NEXT, STACK_TOP, STORED_ON_STACK;
  wire [23:22] rom_1_data;

  or or_1 (or_1_out, PC_t, or_2_out);
  // Probe on STACK_TOP
  // Probe on STACK_TOP
  // Probe on STACK_NEXT
  // Probe on STACK_NEXT
  // Probe on STORED_ON_STACK
  Comparator #(.width(16)) comparator_1 (
    .a(DATA_BUS), .b({16{1'b0}}), .gt(comparator_1_gt), .eq(comparator_1_eq), .lt(comparator_1_lt));
  or or_2 (or_2_out, and_1_out, and_2_out, and_3_out);
  Counter #(.width(16), .max('hffff), .ongoal("stay")) u_PC (
    .load(or_1_out), .D(ADRESS_BUS), .Q(PC), .clk(INC_PC));  // open: count, carry, clr, preset, down
  and and_1 (and_1_out, comparator_1_gt, JPOS);
  and and_2 (and_2_out, comparator_1_eq, JZ);
  and and_3 (and_3_out, comparator_1_lt, JNEG);
  // Probe on DATA_BUS
  // Probe on INSTRUCTION[15:0]
  // Probe on INSTRUCTION[23:16]
  // Probe on SRC
  assign DATA_BUS = PC_SRC ? PC : 16'bz;  // Controlled_Buffer controlled_buffer_1
  assign ADRESS_BUS = PC_ADRESS_SRC ? PC : 16'bz;  // Controlled_Buffer controlled_buffer_2
  // Probe on ADRESS_BUS
  // Probe on ALU_OUT
  // Probe on ALU_OP
  // Probe on ALU_OP
  // Probe on PC
  // Probe on PC
  assign DATA_BUS = OPERAND_SRC ? INSTRUCTION[15:0] : 16'bz;  // Controlled_Buffer controlled_buffer_3
  assign ADRESS_BUS = OPERAND_ADRESS_SRC ? INSTRUCTION[15:0] : 16'bz;  // Controlled_Buffer controlled_buffer_4
  assign DATA_BUS_OUT = ~DEVICE_SRC ? DATA_BUS : 16'bz;  // Controlled_Buffer controlled_buffer_5
  assign DATA_BUS = DEVICE_SRC ? DATA_BUS_IN : 16'bz;  // Controlled_Buffer controlled_buffer_6
  nor nor_1 (HALT, INSTRUCTION[16], INSTRUCTION[17], INSTRUCTION[18], INSTRUCTION[19], INSTRUCTION[20], INSTRUCTION[21], INSTRUCTION[22], INSTRUCTION[23]);
  am08x24arc_cpu_stack am08x24arc_cpu_stack_1 (
    .DATA_IN(DATA_BUS), .STACK_OP(STACK_OP), .TOP(STACK_TOP), .NEXT(STACK_NEXT), .SEL(1'b0), .CLOCK(CLOCK),
    .STACK_OP_EXTRA(STACK_OP_EXTRA), .STORED(STORED_ON_STACK), .INC_PC(INC_PC));
  assign DATA_BUS = STACK_TOP_SRC ? STACK_TOP : 16'bz;  // Controlled_Buffer controlled_buffer_7
  assign ADRESS_BUS = STACK_TOP_ADRESS_SRC ? STACK_TOP : 16'bz;  // Controlled_Buffer controlled_buffer_8
  Decoder #(.select(3), .enable("false")) decoder_1 (
    .out0(OPERAND_SRC), .out1(DEVICE_SRC), .out2(ALU_SRC), .out3(PC_SRC), .out4(STACK_TOP_SRC),
    .out5(STACK_NEXT_SRC), .sel(DATA_BUS_SRC));  // open: out6, out7
  ROM #(.dataWidth(24), .Select("low")) rom_1 (
    .addr(INSTRUCTION[23:16]),
    .data({rom_1_data, ALU_ARG, STACK_OP, STACK_OP_EXTRA, SELECT_DEVICE, DEVICE_ENABLE, JZ, JNEG, JPOS, PC_t, DATA_BUS_SRC, ADRESS_SRC, ALU_OP}));
  assign ADRESS_BUS = STACK_NEXT_ADRES_SRC ? STACK_NEXT : 16'bz;  // Controlled_Buffer controlled_buffer_9
  assign DATA_BUS = STACK_NEXT_SRC ? STACK_NEXT : 16'bz;  // Controlled_Buffer controlled_buffer_10
  Decoder #(.select(3), .enable("false")) decoder_2 (
    .out0(OPERAND_ADRESS_SRC), .out1(ALU_ADRESS_SRC), .out2(PC_ADRESS_SRC), .out3(STACK_TOP_ADRESS_SRC),
    .out4(STACK_NEXT_ADRES_SRC), .sel(ADRESS_SRC));  // open: out5, out6, out7
  am08x24arc_alu am08x24arc_alu_1 (
    .A(STACK_TOP), .B(STACK_NEXT), .C(INSTRUCTION[15:0]), .ALU_ARG(ALU_ARG), .ALU_OP(ALU_OP), .OUT(ALU_OUT));
  assign DATA_BUS = ALU_SRC ? ALU_OUT : 16'bz;  // Controlled_Buffer controlled_buffer_11
  assign ADRESS_BUS = ALU_ADRESS_SRC ? ALU_OUT : 16'bz;  // Controlled_Buffer controlled_buffer_12

  assign BADOP = 1'b0;

  // Other names for the same wires on the sheet: ARGUMENT[15:0] = INSTRUCTION[15:0]; OPCODE[7:0] = INSTRUCTION[23:16];
  //   PROGRAM_COUNTER[15:0] = PC

  // Notes on the sheet:
  //   STACK STATUS
  //   PROGRAM COUNTER
  //   Conditional jumps
  //   STATUS
  //   DATA BUS STATUS
  //   INSTRUCTION STATUS
  //   PC STATUS
  //   ADRESS BUS STATUS
  //   ALU STATUS
  //   OUTPUT
  //   HALT
  //   am08x24arc-cpu
  //   STACK
  //   DATA BUS SRC DECODER
  //   DECODER
  //   contents of rom_1 (hex, n*v repeats v):
  //   0 40000 40180 80000 40200 40280 c0000 42b0 4200 4030 440b0 44080 40100 a0100 40101 40102 40103 40104
  //   40105 40106 40107 40108 40109 400 430 2200 22b0 2102 1a00 1ab0 1902 1200 12b0 a00 ab0 0 8000 8200
  //   ADRESS BUS SRC DECODER
  //   ALU
endmodule

module am08x24arc_alu (
  input  [15:0] A,
  input  [15:0] B,
  input  [15:0] C,
  input  [1:0] ALU_ARG,
  input  [3:0] ALU_OP,
  output [15:0] OUT
);

  wire decoder_1_out0, decoder_1_out1, decoder_1_out2;
  wire [15:0] adder_1_out, and_1_out, controlled_buffer_1_out, controlled_buffer_2_out, n16bit_compare_1_out,
       nand_1_out, negator_1_out, nor_1_out, not_1_out, or_1_out, subtractor_1_out, xor_1_out;

  assign controlled_buffer_1_out = decoder_1_out0 ? A : 16'bz;  // Controlled_Buffer controlled_buffer_1
  assign controlled_buffer_2_out = decoder_1_out0 ? B : 16'bz;  // Controlled_Buffer controlled_buffer_2
  assign controlled_buffer_1_out = decoder_1_out1 ? A : 16'bz;  // Controlled_Buffer controlled_buffer_3
  assign controlled_buffer_2_out = decoder_1_out1 ? C : 16'bz;  // Controlled_Buffer controlled_buffer_4
  assign controlled_buffer_1_out = decoder_1_out2 ? B : 16'bz;  // Controlled_Buffer controlled_buffer_5
  assign controlled_buffer_2_out = decoder_1_out2 ? C : 16'bz;  // Controlled_Buffer controlled_buffer_6
  Decoder #(.select(2), .enable("false")) decoder_1 (
    .out0(decoder_1_out0), .out1(decoder_1_out1), .out2(decoder_1_out2), .sel(ALU_ARG));  // open: out3
  assign not_1_out = ~controlled_buffer_2_out;  // NOT_Gate not_1, 16 bits wide
  Adder #(.width(16)) adder_1 (
    .a(controlled_buffer_2_out), .b(controlled_buffer_1_out), .out(adder_1_out));  // open: cin, cout
  Subtractor #(.width(16)) subtractor_1 (
    .a(controlled_buffer_2_out), .b(controlled_buffer_1_out), .out(subtractor_1_out));  // open: bin, bout
  _16bit_compare u_16bit_compare_1 (
    .A(controlled_buffer_2_out), .B(controlled_buffer_1_out), .OUT(n16bit_compare_1_out));
  Negator #(.width(16)) negator_1 (.in(controlled_buffer_2_out), .out(negator_1_out));
  assign and_1_out = controlled_buffer_2_out & controlled_buffer_1_out;  // AND_Gate and_1, 16 bits wide
  assign or_1_out = controlled_buffer_2_out | controlled_buffer_1_out;  // OR_Gate or_1, 16 bits wide
  assign nand_1_out = ~(controlled_buffer_2_out & controlled_buffer_1_out);  // NAND_Gate nand_1, 16 bits wide
  assign nor_1_out = ~(controlled_buffer_2_out | controlled_buffer_1_out);  // NOR_Gate nor_1, 16 bits wide
  assign xor_1_out = controlled_buffer_2_out ^ controlled_buffer_1_out;  // XOR_Gate xor_1, 16 bits wide
  Multiplexer #(.select(4), .width(16), .enable("false")) multiplexer_1 (
    .in0(adder_1_out), .in1(subtractor_1_out), .in2(n16bit_compare_1_out), .in3(negator_1_out),
    .in4(not_1_out), .in5(and_1_out), .in6(or_1_out), .in7(nand_1_out), .in8(nor_1_out), .in9(xor_1_out),
    .out(OUT), .sel(ALU_OP));  // open: in10, in11, in12, in13, in14, in15

  // Notes on the sheet:
  //   ALU interface
endmodule

module am08x24arc_cpu_stack (
  input  [15:0] DATA_IN,
  input  [1:0] STACK_OP,
  input  [1:0] STACK_OP_EXTRA,
  input  SEL,
  input  CLOCK,
  input  INC_PC,
  output [15:0] STORED,
  output [15:0] TOP,
  output [15:0] NEXT
);

  wire and_1_out, and_2_out, and_3_out, and_4_out, and_5_out, and_6_out, decoder_1_out2, DROP, jstack_1_p8,
       not_1_out, PUSH, SET_NEXT, SET_TOP, SWAP;

  Decoder #(.select(2), .enable("false")) decoder_1 (
    .out1(PUSH), .out2(decoder_1_out2), .out3(SWAP), .sel(STACK_OP));  // open: out0
  Decoder #(.select(2), .enable("false")) decoder_2 (
    .out1(SET_TOP), .out2(SET_NEXT), .sel(STACK_OP_EXTRA));  // open: out0, out3
  Register #(.width(1), .Select("low")) register_1 (.D(decoder_1_out2), .Q(DROP), .clk(CLOCK));  // open: en, clr
  and and_1 (and_1_out, PUSH, not_1_out);
  and and_2 (and_2_out, DROP, INC_PC);
  and and_3 (and_3_out, SWAP, not_1_out);
  and and_4 (and_4_out, SET_TOP, not_1_out);
  and and_5 (and_5_out, SET_NEXT, not_1_out);
  not not_1 (not_1_out, CLOCK);
  // JStack jstack_1: pin names not known; wires that end beside it: DATA_IN, and_1_out, and_2_out, and_3_out, and_4_out, and_5_out, SEL, jstack_1_p8, TOP, NEXT, STORED
  or or_1 (jstack_1_p8, CLOCK, and_6_out);
  and and_6 (and_6_out, DROP, INC_PC);

  // Notes on the sheet:
  //   am08x24arc-stack
endmodule

module am08x24arc_clock (
  input  HALT,
  input  BADOP,
  output CLOCK,
  output INC_PC
);

  wire and_1_out, clock_1_out, not_1_out, t_ff_1_q, t_ff_1_qn, t_ff_2_q, t_ff_2_qn;

  Clock clock_1 (.out(clock_1_out));
  LED led_1 (.in(BADOP));
  and and_1 (and_1_out, clock_1_out, ~HALT, ~BADOP);  // AND_Gate
  not not_1 (not_1_out, and_1_out);
  T_Flip_Flop t_ff_1 (.clk(not_1_out), .T(1'b1), .Q(t_ff_1_q), .Qn(t_ff_1_qn));  // open: preset, reset
  T_Flip_Flop #(.Pre_Clr_Positions("LEGACY"), .enable("true")) t_ff_2 (
    .clk(and_1_out), .T(1'b1), .Q(t_ff_2_q), .Qn(t_ff_2_qn));  // open: preset, reset, en
  and and_2 (CLOCK, and_1_out, t_ff_1_qn, t_ff_2_q);
  and and_3 (INC_PC, t_ff_2_qn, t_ff_1_q, and_1_out);

  // Notes on the sheet:
  //   am08x24arc-clock
endmodule

module am08x24arc_gpu_core (
  input  CLOCK,
  input  INC_PC,
  input  [15:0] DATA_BUS_IN,
  output [15:0] DATA_BUS_OUT,
  output HALT,
  output BADOP,
  output [15:0] STACK_TOP,
  output SELECT_DEVICE,
  output DEVICE_SRC,
  output DEVICE_ENABLE
);

  wire _24BIT_INSTUCTION, ALU_SRC, and_1_out, and_2_out, and_3_out, and_4_out, and_5_out, comparator_1_eq,
       comparator_1_gt, comparator_1_lt, JNEG, JPOS, JZ, not_1_out, OPERAND_SRC, or_2_out, PC_ADRESS_WRITE,
       PC_SRC, STACK_NEXT_SRC, STACK_POP, STACK_SWAP, STACK_TOP_SRC;
  wire [3:0] ALU_OP;
  wire [10:3] controlled_buffer_7_out;
  wire [15:0] ALU_OUT, ARGUMENT, controlled_buffer_1_out, DATA_BUS, PROGRAM_COUNTER, STACK_NEXT;
  wire [22:16] INSTRUCTION;

  assign controlled_buffer_1_out = _24BIT_INSTUCTION ? STACK_TOP : 16'bz;  // Controlled_Buffer controlled_buffer_1
  assign controlled_buffer_1_out = ~_24BIT_INSTUCTION ? DATA_BUS : 16'bz;  // Controlled_Buffer controlled_buffer_2
  and and_1 (and_1_out, _24BIT_INSTUCTION, INSTRUCTION[19], or_2_out);
  and and_2 (and_2_out, ~_24BIT_INSTUCTION, INSTRUCTION[19]);  // AND_Gate
  or or_1 (PC_ADRESS_WRITE, and_2_out, and_1_out);
  Comparator #(.width(16)) comparator_1 (
    .a(STACK_NEXT), .b({16{1'b0}}), .gt(comparator_1_gt), .eq(comparator_1_eq), .lt(comparator_1_lt));
  or or_2 (or_2_out, and_3_out, and_4_out, and_5_out);
  Counter #(.width(16), .max('hffff), .ongoal("stay")) PC (
    .load(PC_ADRESS_WRITE), .D(controlled_buffer_1_out), .Q(PROGRAM_COUNTER), .clk(INC_PC));  // open: count, carry, clr, preset, down
  and and_3 (and_3_out, comparator_1_gt, JPOS);
  and and_4 (and_4_out, comparator_1_eq, JZ);
  assign DATA_BUS_OUT = ~DEVICE_SRC ? DATA_BUS : 16'bz;  // Controlled_Buffer controlled_buffer_3
  assign DATA_BUS = DEVICE_SRC ? DATA_BUS_IN : 16'bz;  // Controlled_Buffer controlled_buffer_4
  and and_5 (and_5_out, comparator_1_lt, JNEG);
  assign DATA_BUS = PC_SRC ? PROGRAM_COUNTER : 16'bz;  // Controlled_Buffer controlled_buffer_5
  Decoder #(.select(3), .enable("false")) decoder_1 (
    .out0(OPERAND_SRC), .out1(DEVICE_SRC), .out2(ALU_SRC), .out3(PC_SRC), .out6(STACK_TOP_SRC),
    .out7(STACK_NEXT_SRC), .sel(INSTRUCTION[18:16]));  // open: out4, out5
  nor nor_1 (HALT, INSTRUCTION[16], INSTRUCTION[17], INSTRUCTION[18], INSTRUCTION[19], DEVICE_ENABLE, SELECT_DEVICE, INSTRUCTION[22], _24BIT_INSTUCTION);
  assign DATA_BUS = OPERAND_SRC ? ARGUMENT : 16'bz;  // Controlled_Buffer controlled_buffer_6
  ROM #(.addrWidth(16), .dataWidth(24), .Select("low")) Instruction_ROM (
    .addr(PROGRAM_COUNTER),
    .data({_24BIT_INSTUCTION, INSTRUCTION[22], SELECT_DEVICE, DEVICE_ENABLE, INSTRUCTION[19:16], ARGUMENT}));
  assign {STACK_POP, STACK_SWAP, JZ, JNEG, JPOS, controlled_buffer_7_out[10:9], ALU_OP[3], controlled_buffer_7_out[7:3], ALU_OP[2:0]} = _24BIT_INSTUCTION ? ARGUMENT : 16'bz;  // Controlled_Buffer controlled_buffer_7
  am08x24arc_gpu_stack am08x24arc_gpu_stack_1 (
    .DATA_IN(DATA_BUS), .PUSH(INSTRUCTION[22]), .POP(STACK_POP), .SWAP(STACK_SWAP), .TOP(STACK_TOP),
    .NEXT(STACK_NEXT), .SEL(1'b0), .CLOCK(CLOCK));
  not not_1 (not_1_out, _24BIT_INSTUCTION);
  assign {STACK_POP, STACK_SWAP, JZ, JNEG, JPOS, controlled_buffer_7_out[10:9], ALU_OP[3], controlled_buffer_7_out[7:3], ALU_OP[2:0]} = not_1_out ? {16{1'b0}} : 16'bz;  // Controlled_Buffer controlled_buffer_8
  assign DATA_BUS = STACK_TOP_SRC ? STACK_TOP : 16'bz;  // Controlled_Buffer controlled_buffer_9
  assign DATA_BUS = STACK_NEXT_SRC ? STACK_NEXT : 16'bz;  // Controlled_Buffer controlled_buffer_10
  // am08x24arc_alu am08x24arc_alu_1: pin names not known; wires that end beside it: STACK_TOP, STACK_NEXT, ALU_OP, ALU_OUT
  assign DATA_BUS = ALU_SRC ? ALU_OUT : 16'bz;  // Controlled_Buffer controlled_buffer_11

  assign BADOP = 1'b0;

  // Other names for the same wires on the sheet: INSTRUCTION (some bits) = {_24BIT_INSTUCTION, SELECT_DEVICE, DEVICE_ENABLE, ARGUMENT};
  //   OPCODE[7:0] = {_24BIT_INSTUCTION, INSTRUCTION[22], SELECT_DEVICE, DEVICE_ENABLE, INSTRUCTION[19:16]};
  //   SRC[2:0] = INSTRUCTION[18:16]; PC = INSTRUCTION[19]; STACK_PUSH = INSTRUCTION[22]

  // Notes on the sheet:
  //   OUTPUT
  //   PROGRAM COUNTER
  //   Conditional jumps
  //   HALT
  //   SOURCE DECODER
  //   contents of Instruction_ROM (hex, n*v repeats v):
  //   8004b 804000 d10000 c20002 40000a 8e2000 808000 808000 808000 80002 4*808000 400002 c20000 804000
  //   808000 804000 808000 8e3800 4*808000 200000 400004 400000 970000 808000 808000 400003 c30000 80001
  //   808000 200001 400001 d10000 804000 808000 400002 d10000 804000 808000 400003 d10000 804000 808000
  //   200007 400000 970000 808000 808000 400000 970000 808000 808000 400000 970000 808000 808000 970000
  //   8004b 808000 808000 808000 400020 0 8004b 808000 808000 808000 400030 0 8004b 200000 400001 400000
  //   970000 808000 808000 200000 d10000 400005 c20002 400015 8e2000 808000 808000 808000 400006 c20002
  //   40003f 8e2000 808000 808000 808000 400007 c20002 400045 8e2000 4*808000 80051
  //   am08x24arc-gpu-core
  //   DECODER
  //   STACK
  //   ALU
endmodule

module am08x24arc_gpu_stack (
  input  [15:0] DATA_IN,
  input  PUSH,
  input  POP,
  input  SWAP,
  input  SEL,
  input  CLOCK,
  output [15:0] TOP,
  output [15:0] NEXT
);

  _16bit_stack8 u_16bit_stack8_1 (
    .DATA_IN(DATA_IN), .PUSH(PUSH), .POP(POP), .SWAP(SWAP), .TOP(TOP), .NEXT(NEXT), .SEL(SEL), .CLOCK(CLOCK),
    .CARRY_IN({16{1'b0}}));  // open: CARRY_OUT, LAST

  // Other names for the same wires on the sheet: POP_OP = POP; PUSH_OP = PUSH; SWAP_OP = SWAP

  // Notes on the sheet:
  //   am08x24arc-gpu-stack
endmodule

module am08x24arc_gpu_main_core (
  input  [15:0] in_1,
  output [15:0] out_2,
  output [15:0] out_3,
  output CLOCK,
  output DEVICE_SELECT,
  output DEVICE_SRC,
  output DEVICE_ENABLE
);

  wire BADOP, HALT, INC_PC;
  wire [15:0] PC;
  wire [23:0] INSTRUCTION;

  am08x24arc_cpu am08x24arc_cpu_1 (
    .DATA_BUS_OUT(out_2), .ADRESS_BUS(out_3), .CLOCK(CLOCK), .INC_PC(INC_PC), .HALT(HALT), .BADOP(BADOP),
    .DEVICE_SRC(DEVICE_SRC), .SELECT_DEVICE(DEVICE_SELECT), .DEVICE_ENABLE(DEVICE_ENABLE),
    .DATA_BUS_IN(in_1), .PC(PC), .INSTRUCTION(INSTRUCTION));
  am08x24arc_clock am08x24arc_clock_1 (.HALT(HALT), .BADOP(BADOP), .CLOCK(CLOCK), .INC_PC(INC_PC));
  ROM #(.addrWidth(16), .dataWidth(24), .Select("low")) Instruction_ROM (.addr(PC), .data(INSTRUCTION));

  // Other names for the same wires on the sheet: ADRESS_BUS[15:0] = out_3; DATA_BUS_IN[15:0] = in_1;
  //   DATA_BUS_OUT[15:0] = out_2

  // Notes on the sheet:
  //   am08x24arc-gpu-main-core
  //   contents of Instruction_ROM (hex, n*v repeats v):
  //   16002a b0000 1a0005 30000 160001 30000 30000 10003 c0000 60000 30000 60000 30000 170000 30000 30000
  //   10004 80000 30000 20000 10003 160001 30000 230001 b0001 b0002 b0003 230007 80000 30000 80000 30000
  //   80000 30000 70000 16002a 30000 30000 0 30000 30000 0 230000 10001 80000 30000 b0000 10005 1a000e
  //   30000 10006 1a0024 30000 10007 1a0027 30000 30000 16002e
endmodule

module _16bit_decimal_display_controller (
  input  [15:0] DATA_IN,
  input  CLOCK,
  output [3:0] DIGIT_4,
  output [3:0] DIGIT_3,
  output [3:0] DIGIT_2,
  output [3:0] DIGIT_1,
  output [3:0] DIGIT_0
);

  wire [15:0] divider_1_out, divider_2_out, divider_3_out, divider_4_out, register_1_q;
  wire [15:4] divider_1_rem, divider_2_rem, divider_3_rem, divider_4_rem, divider_5_rem;

  Register #(.width(16), .Select("low")) register_1 (.D(DATA_IN), .Q(register_1_q), .clk(CLOCK));  // open: en, clr
  Divider #(.width(16)) divider_1 (
    .a(register_1_q), .b(16'ha), .out(divider_1_out), .upper({16{1'b0}}), .rem({divider_1_rem, DIGIT_0}));
  Divider #(.width(16)) divider_2 (
    .a(divider_1_out), .b(16'ha), .out(divider_2_out), .upper({16{1'b0}}), .rem({divider_2_rem, DIGIT_1}));
  Divider #(.width(16)) divider_3 (
    .a(divider_2_out), .b(16'ha), .out(divider_3_out), .upper({16{1'b0}}), .rem({divider_3_rem, DIGIT_2}));
  Divider #(.width(16)) divider_4 (
    .a(divider_3_out), .b(16'ha), .out(divider_4_out), .upper({16{1'b0}}), .rem({divider_4_rem, DIGIT_3}));
  Divider #(.width(16)) divider_5 (
    .a(divider_4_out), .b(16'ha), .upper({16{1'b0}}), .rem({divider_5_rem, DIGIT_4}));  // open: out
endmodule

module _16x16_led_matrix (
  input  [15:0] DATA_IN,
  input  [15:0] ADRESS,
  input  BLOCK,
  input  CLOCK,
  input  SEL,
  output [15:0] out_6,
  output [15:0] out_7,
  output [15:0] out_8,
  output [15:0] out_9,
  output [15:0] out_10,
  output [15:0] out_11,
  output [15:0] out_12,
  output [15:0] out_13,
  output [15:0] out_14,
  output [15:0] out_15,
  output [15:0] out_16,
  output [15:0] out_17,
  output [15:0] out_18,
  output [15:0] out_19,
  output [15:0] out_20,
  output [15:0] out_21
);

  wire and_1_out, and_2_out, and_3_out, and_4_out, and_5_out, and_6_out, and_7_out, and_8_out, and_9_out,
       and_10_out, and_11_out, and_12_out, and_13_out, and_14_out, and_15_out, and_16_out, decoder_1_out0,
       decoder_1_out1, decoder_1_out2, decoder_1_out3, decoder_1_out4, decoder_1_out5, decoder_1_out6,
       decoder_1_out7, decoder_1_out8, decoder_1_out9, decoder_1_out10, decoder_1_out11, decoder_1_out12,
       decoder_1_out13, decoder_1_out14, decoder_1_out15;

  Decoder #(.select(4), .enable("false")) decoder_1 (
    .out0(decoder_1_out0), .out1(decoder_1_out1), .out2(decoder_1_out2), .out3(decoder_1_out3),
    .out4(decoder_1_out4), .out5(decoder_1_out5), .out6(decoder_1_out6), .out7(decoder_1_out7),
    .out8(decoder_1_out8), .out9(decoder_1_out9), .out10(decoder_1_out10), .out11(decoder_1_out11),
    .out12(decoder_1_out12), .out13(decoder_1_out13), .out14(decoder_1_out14), .out15(decoder_1_out15),
    .sel(ADRESS[3:0]));
  and and_1 (and_1_out, decoder_1_out15, BLOCK);
  and and_2 (and_2_out, decoder_1_out14, BLOCK);
  and and_3 (and_3_out, decoder_1_out13, BLOCK);
  and and_4 (and_4_out, decoder_1_out12, BLOCK);
  and and_5 (and_5_out, decoder_1_out11, BLOCK);
  and and_6 (and_6_out, decoder_1_out10, BLOCK);
  and and_7 (and_7_out, decoder_1_out9, BLOCK);
  and and_8 (and_8_out, decoder_1_out8, BLOCK);
  and and_9 (and_9_out, decoder_1_out7, BLOCK);
  and and_10 (and_10_out, decoder_1_out6, BLOCK);
  and and_11 (and_11_out, decoder_1_out5, BLOCK);
  and and_12 (and_12_out, decoder_1_out4, BLOCK);
  and and_13 (and_13_out, decoder_1_out3, BLOCK);
  and and_14 (and_14_out, decoder_1_out2, BLOCK);
  and and_15 (and_15_out, decoder_1_out1, BLOCK);
  and and_16 (and_16_out, decoder_1_out0, BLOCK);
  Register #(.width(16), .Select("low")) register_1 (
    .D(DATA_IN), .en(and_1_out), .Q(out_6), .clk(CLOCK), .cs(SEL));  // open: clr, preset
  Register #(.width(16), .Select("low")) register_2 (
    .D(DATA_IN), .en(and_2_out), .Q(out_7), .clk(CLOCK), .cs(SEL));  // open: clr, preset
  Register #(.width(16), .Select("low")) register_3 (
    .D(DATA_IN), .en(and_3_out), .Q(out_8), .clk(CLOCK), .cs(SEL));  // open: clr, preset
  Register #(.width(16), .Select("low")) register_4 (
    .D(DATA_IN), .en(and_4_out), .Q(out_9), .clk(CLOCK), .cs(SEL));  // open: clr, preset
  Register #(.width(16), .Select("low")) register_5 (
    .D(DATA_IN), .en(and_5_out), .Q(out_10), .clk(CLOCK), .cs(SEL));  // open: clr, preset
  Register #(.width(16), .Select("low")) register_6 (
    .D(DATA_IN), .en(and_6_out), .Q(out_11), .clk(CLOCK), .cs(SEL));  // open: clr, preset
  Register #(.width(16), .Select("low")) register_7 (
    .D(DATA_IN), .en(and_7_out), .Q(out_12), .clk(CLOCK), .cs(SEL));  // open: clr, preset
  Register #(.width(16), .Select("low")) register_8 (
    .D(DATA_IN), .en(and_8_out), .Q(out_13), .clk(CLOCK), .cs(SEL));  // open: clr, preset
  Register #(.width(16), .Select("low")) register_9 (
    .D(DATA_IN), .en(and_9_out), .Q(out_14), .clk(CLOCK), .cs(SEL));  // open: clr, preset
  Register #(.width(16), .Select("low")) register_10 (
    .D(DATA_IN), .en(and_10_out), .Q(out_15), .clk(CLOCK), .cs(SEL));  // open: clr, preset
  Register #(.width(16), .Select("low")) register_11 (
    .D(DATA_IN), .en(and_11_out), .Q(out_16), .clk(CLOCK), .cs(SEL));  // open: clr, preset
  Register #(.width(16), .Select("low")) register_12 (
    .D(DATA_IN), .en(and_12_out), .Q(out_17), .clk(CLOCK), .cs(SEL));  // open: clr, preset
  Register #(.width(16), .Select("low")) register_13 (
    .D(DATA_IN), .en(and_13_out), .Q(out_18), .clk(CLOCK), .cs(SEL));  // open: clr, preset
  Register #(.width(16), .Select("low")) register_14 (
    .D(DATA_IN), .en(and_14_out), .Q(out_19), .clk(CLOCK), .cs(SEL));  // open: clr, preset
  Register #(.width(16), .Select("low")) register_15 (
    .D(DATA_IN), .en(and_15_out), .Q(out_20), .clk(CLOCK), .cs(SEL));  // open: clr, preset
  Register #(.width(16), .Select("low")) register_16 (
    .D(DATA_IN), .en(and_16_out), .Q(out_21), .clk(CLOCK), .cs(SEL));  // open: clr, preset

  // Other names for the same wires on the sheet: DATA_BUS[15:0] = DATA_IN
endmodule

module _16x_device_selector (
  input  [15:0] DEVICE,
  input  DEVICE_SELECT,
  input  CLOCK,
  output out_4,
  output out_5,
  output out_6,
  output out_7,
  output out_8,
  output out_9,
  output out_10,
  output out_11,
  output out_12,
  output out_13,
  output out_14,
  output out_15,
  output out_16,
  output out_17,
  output out_18,
  output out_19
);

  wire and_1_out;
  wire [15:0] register_1_q;

  and and_1 (and_1_out, CLOCK, DEVICE_SELECT);
  Register #(.width(16), .Select("low")) register_1 (.D(DEVICE), .Q(register_1_q), .clk(and_1_out));  // open: en, clr
  Decoder #(.select(4), .enable("false")) decoder_1 (
    .out0(out_4), .out1(out_5), .out2(out_6), .out3(out_7), .out4(out_8), .out5(out_9), .out6(out_10),
    .out7(out_11), .out8(out_12), .out9(out_13), .out10(out_14), .out11(out_15), .out12(out_16),
    .out13(out_17), .out14(out_18), .out15(out_19), .sel(register_1_q[3:0]));
endmodule

module _8x_device_selector (
  input  [15:0] DEVICE,
  input  DEVICE_SELECT,
  input  CLOCK,
  output out_4,
  output out_5,
  output out_6,
  output out_7,
  output out_8,
  output out_9,
  output out_10,
  output out_11
);

  wire and_1_out;
  wire [15:0] register_1_q;

  Register #(.width(16), .Select("low")) register_1 (.D(DEVICE), .Q(register_1_q), .clk(and_1_out));  // open: en, clr
  and and_1 (and_1_out, CLOCK, DEVICE_SELECT);
  Decoder #(.select(3), .enable("false")) decoder_1 (
    .out0(out_4), .out1(out_5), .out2(out_6), .out3(out_7), .out4(out_8), .out5(out_9), .out6(out_10),
    .out7(out_11), .sel(register_1_q[2:0]));
endmodule

// 16bit-2thread-register3
module _16bit_2thread_register (
  input  SEL,
  input  CLOCK_0,
  input  CLOCK_1,
  input  ENABLE_0,
  input  ENABLE_1,
  input  DEVICE_SRC_0,
  input  DEVICE_SRC_1,
  input  [15:0] DATA_BUS_0_IN,
  input  [15:0] DATA_BUS_1_IN,
  output [15:0] STORED,
  output [15:0] DATA_BUS_0_OUT,
  output [15:0] DATA_BUS_1_OUT
);

  wire and_1_out, and_2_out, and_3_out, and_4_out, and_5_out, and_6_out, not_1_out, not_2_out, or_1_out;
  wire [15:0] controlled_buffer_3_out, DATA_BUS_0, DATA_BUS_1;

  assign DATA_BUS_0 = ~DEVICE_SRC_0 ? DATA_BUS_0_IN : 16'bz;  // Controlled_Buffer controlled_buffer_1
  assign DATA_BUS_0_OUT = DEVICE_SRC_0 ? DATA_BUS_0 : 16'bz;  // Controlled_Buffer controlled_buffer_2
  and and_1 (and_1_out, CLOCK_0, ENABLE_0);
  not not_1 (not_1_out, DEVICE_SRC_0);
  and and_2 (and_2_out, not_1_out, and_1_out);
  assign controlled_buffer_3_out = and_2_out ? DATA_BUS_0 : 16'bz;  // Controlled_Buffer controlled_buffer_3
  and and_3 (and_3_out, CLOCK_1, ENABLE_1);
  not not_2 (not_2_out, DEVICE_SRC_1);
  and and_4 (and_4_out, and_3_out, not_2_out);
  assign controlled_buffer_3_out = and_4_out ? DATA_BUS_1 : 16'bz;  // Controlled_Buffer controlled_buffer_4
  Register #(.width(16), .Select("low")) register_1 (
    .D(controlled_buffer_3_out), .Q(STORED), .clk(or_1_out), .cs(SEL));  // open: en, clr, preset
  or or_1 (or_1_out, and_4_out, and_2_out);
  assign DATA_BUS_0 = and_5_out ? STORED : 16'bz;  // Controlled_Buffer controlled_buffer_5
  and and_5 (and_5_out, ENABLE_0, DEVICE_SRC_0);
  assign DATA_BUS_1 = ~DEVICE_SRC_1 ? DATA_BUS_1_IN : 16'bz;  // Controlled_Buffer controlled_buffer_6
  assign DATA_BUS_1_OUT = DEVICE_SRC_1 ? DATA_BUS_1 : 16'bz;  // Controlled_Buffer controlled_buffer_7
  assign DATA_BUS_1 = and_6_out ? STORED : 16'bz;  // Controlled_Buffer controlled_buffer_8
  and and_6 (and_6_out, ENABLE_1, DEVICE_SRC_1);
endmodule

module _16bit_2semi_thread_ram (
  input  WRONG_INPUT,
  input  CLOCK_0,
  input  CLOCK_1,
  input  ENABLE_0,
  input  ENABLE_1,
  input  DEVICE_SRC_0,
  input  DEVICE_SRC_1,
  input  [15:0] DATA_BUS_0_IN,
  input  [15:0] DATA_BUS_1_IN,
  input  [15:0] ADRESS_0,
  input  [15:0] ADRESS_1,
  output [15:0] DATA_BUS_0_OUT,
  output [15:0] DATA_BUS_1_OUT
);

  wire and_1_out, and_2_out, and_3_out, and_4_out, and_5_out, and_6_out, or_1_out;
  wire [15:0] controlled_buffer_1_out, controlled_buffer_3_out, DATA_BUS_0, DATA_BUS_1, ram_1_data;

  assign controlled_buffer_1_out = ENABLE_0 ? ADRESS_0 : 16'bz;  // Controlled_Buffer controlled_buffer_1
  assign controlled_buffer_1_out = ENABLE_1 ? ADRESS_1 : 16'bz;  // Controlled_Buffer controlled_buffer_2
  and and_1 (and_1_out, ENABLE_0, ~DEVICE_SRC_0);  // AND_Gate
  assign controlled_buffer_3_out = and_1_out ? DATA_BUS_0 : 16'bz;  // Controlled_Buffer controlled_buffer_3
  assign controlled_buffer_3_out = and_2_out ? DATA_BUS_1 : 16'bz;  // Controlled_Buffer controlled_buffer_4
  and and_2 (and_2_out, ~DEVICE_SRC_1, ENABLE_1);  // AND_Gate
  assign DATA_BUS_0 = ~DEVICE_SRC_0 ? DATA_BUS_0_IN : 16'bz;  // Controlled_Buffer controlled_buffer_5
  assign DATA_BUS_0_OUT = DEVICE_SRC_0 ? DATA_BUS_0 : 16'bz;  // Controlled_Buffer controlled_buffer_6
  assign DATA_BUS_1 = ~DEVICE_SRC_1 ? DATA_BUS_1_IN : 16'bz;  // Controlled_Buffer controlled_buffer_7
  RAM #(.addrWidth(16), .dataWidth(16), .bus("separate"), .Select("low")) ram_1 (
    .addr(controlled_buffer_1_out), .din(controlled_buffer_3_out), .data(ram_1_data), .clk(or_1_out));  // open: str, sel, ld, clr
  or or_1 (or_1_out, CLOCK_1, CLOCK_0);
  assign DATA_BUS_1_OUT = DEVICE_SRC_1 ? DATA_BUS_1 : 16'bz;  // Controlled_Buffer controlled_buffer_8
  or or_2 (WRONG_INPUT, and_3_out, and_6_out);
  and and_3 (and_3_out, ENABLE_0, DEVICE_SRC_0, DEVICE_SRC_1, ENABLE_1);
  and and_4 (and_4_out, ENABLE_0, DEVICE_SRC_0);
  assign DATA_BUS_0 = and_4_out ? ram_1_data : 16'bz;  // Controlled_Buffer controlled_buffer_9
  assign DATA_BUS_1 = and_5_out ? ram_1_data : 16'bz;  // Controlled_Buffer controlled_buffer_10
  and and_5 (and_5_out, DEVICE_SRC_1, ENABLE_1);
  and and_6 (and_6_out, ENABLE_0, ENABLE_1);
endmodule

module _4x_device_selector (
  input  [15:0] DEVICE,
  input  DEVICE_SELECT,
  input  CLOCK,
  output out_4,
  output out_5,
  output out_6,
  output out_7
);

  wire and_1_out;
  wire [15:0] register_1_q;

  and and_1 (and_1_out, CLOCK, DEVICE_SELECT);
  Register #(.width(16), .Select("low")) register_1 (.D(DEVICE), .Q(register_1_q), .clk(and_1_out));  // open: en, clr
  Decoder #(.select(2), .enable("false")) decoder_1 (
    .out0(out_4), .out1(out_5), .out2(out_6), .out3(out_7), .sel(register_1_q[1:0]));
endmodule

module am08x24arc_devices (
  input  SEL
);

  wire and_1_out, and_2_out, and_3_out, and_4_out, and_5_out, and_6_out, CLOCK, comparator_1_eq,
       DEVICE_ENABLE, DEVICE_SRC, not_1_out, not_2_out, undriven, undriven_2, undriven_3, undriven_4,
       undriven_5;
  wire [3:0] n16bit_decimal_display_controller_1_digit_0, n16bit_decimal_display_controller_1_digit_1,
       n16bit_decimal_display_controller_1_digit_2, n16bit_decimal_display_controller_1_digit_3,
       n16bit_decimal_display_controller_1_digit_4;
  wire [15:0] DATA_BUS, Instruction_ROM_data, n16x16_led_matrix_1_out_6, n16x16_led_matrix_1_out_7,
       n16x16_led_matrix_1_out_8, n16x16_led_matrix_1_out_9, n16x16_led_matrix_1_out_10,
       n16x16_led_matrix_1_out_11, n16x16_led_matrix_1_out_12, n16x16_led_matrix_1_out_13,
       n16x16_led_matrix_1_out_14, n16x16_led_matrix_1_out_15, n16x16_led_matrix_1_out_16,
       n16x16_led_matrix_1_out_17, n16x16_led_matrix_1_out_18, n16x16_led_matrix_1_out_19,
       n16x16_led_matrix_1_out_20, n16x16_led_matrix_1_out_21, STACK_TOP;

  Hex_Digit_Display hex_digit_display_1 (.value(n16bit_decimal_display_controller_1_digit_4));  // open: dp
  _16bit_decimal_display_controller u_16bit_decimal_display_controller_1 (
    .DATA_IN(DATA_BUS), .DIGIT_4(n16bit_decimal_display_controller_1_digit_4),
    .DIGIT_3(n16bit_decimal_display_controller_1_digit_3),
    .DIGIT_2(n16bit_decimal_display_controller_1_digit_2),
    .DIGIT_1(n16bit_decimal_display_controller_1_digit_1),
    .DIGIT_0(n16bit_decimal_display_controller_1_digit_0), .CLOCK(and_1_out));
  and and_1 (and_1_out, undriven, DEVICE_ENABLE, CLOCK);
  Hex_Digit_Display hex_digit_display_2 (.value(n16bit_decimal_display_controller_1_digit_2));  // open: dp
  Hex_Digit_Display hex_digit_display_3 (.value(n16bit_decimal_display_controller_1_digit_3));  // open: dp
  Hex_Digit_Display hex_digit_display_4 (.value(n16bit_decimal_display_controller_1_digit_1));  // open: dp
  Hex_Digit_Display hex_digit_display_5 (.value(n16bit_decimal_display_controller_1_digit_0));  // open: dp
  and and_2 (and_2_out, undriven_3, DEVICE_ENABLE, CLOCK);
  not not_1 (not_1_out, DEVICE_ENABLE);
  TTY tty_1 (.data(DATA_BUS[6:0]), .clk(and_2_out), .clr(and_3_out));  // open: we
  and and_3 (and_3_out, and_2_out, comparator_1_eq);
  Comparator #(.width(9)) comparator_1 (.a(DATA_BUS[15:7]), .b({9{1'b1}}), .eq(comparator_1_eq));  // open: gt, lt
  // Probe on DATA_BUS
  ROM #(.addrWidth(16), .dataWidth(16), .Select("low")) Instruction_ROM (
    .addr(STACK_TOP), .data(Instruction_ROM_data), .sel(not_1_out));
  assign DATA_BUS = and_4_out ? Instruction_ROM_data : 16'bz;  // Controlled_Buffer controlled_buffer_1
  and and_4 (and_4_out, DEVICE_ENABLE, DEVICE_SRC, undriven_2);
  and and_5 (and_5_out, undriven_4, DEVICE_ENABLE);
  not not_2 (not_2_out, and_5_out);
  and and_6 (and_6_out, undriven_5, DEVICE_ENABLE);
  RAM #(.addrWidth(16), .dataWidth(16), .Select("low")) ram_1 (
    .addr(STACK_TOP), .data(DATA_BUS), .sel(not_2_out), .clk(CLOCK), .ld(DEVICE_SRC));  // open: clr
  DotMatrix #(.inputtype("row"), .matrixcols(16), .matrixrows(16)) dotmatrix_1 (
    .row0(n16x16_led_matrix_1_out_6), .row1(n16x16_led_matrix_1_out_7), .row2(n16x16_led_matrix_1_out_8),
    .row3(n16x16_led_matrix_1_out_9), .row4(n16x16_led_matrix_1_out_10), .row5(n16x16_led_matrix_1_out_11),
    .row6(n16x16_led_matrix_1_out_12), .row7(n16x16_led_matrix_1_out_13), .row8(n16x16_led_matrix_1_out_14),
    .row9(n16x16_led_matrix_1_out_15), .row10(n16x16_led_matrix_1_out_16),
    .row11(n16x16_led_matrix_1_out_17), .row12(n16x16_led_matrix_1_out_18),
    .row13(n16x16_led_matrix_1_out_19), .row14(n16x16_led_matrix_1_out_20), .row15(n16x16_led_matrix_1_out_21));
  _16x16_led_matrix u_16x16_led_matrix_1 (
    .DATA_IN(DATA_BUS), .ADRESS(STACK_TOP), .BLOCK(and_6_out), .CLOCK(CLOCK),
    .out_6(n16x16_led_matrix_1_out_6), .out_7(n16x16_led_matrix_1_out_7), .out_8(n16x16_led_matrix_1_out_8),
    .out_9(n16x16_led_matrix_1_out_9), .out_10(n16x16_led_matrix_1_out_10),
    .out_11(n16x16_led_matrix_1_out_11), .out_12(n16x16_led_matrix_1_out_12),
    .out_13(n16x16_led_matrix_1_out_13), .out_14(n16x16_led_matrix_1_out_14),
    .out_15(n16x16_led_matrix_1_out_15), .out_16(n16x16_led_matrix_1_out_16),
    .out_17(n16x16_led_matrix_1_out_17), .out_18(n16x16_led_matrix_1_out_18),
    .out_19(n16x16_led_matrix_1_out_19), .out_20(n16x16_led_matrix_1_out_20),
    .out_21(n16x16_led_matrix_1_out_21), .SEL(SEL));

  // Notes on the sheet:
  //   contents of Instruction_ROM (hex, n*v repeats v):
  //   8*ffff 4003 fff8 f fff8 f fff8 1f fff8 1f fff8 f fffc f fffc 2003 fff8 6003 fff0 6003 fff0 4003 fff0
  //   4003 fff8 8003 ffff 8003 ffff 8003 ffff 7 ffff 7 fffe 7 fffe 7 fffe f ffff 800f ffff c00f ffff f01f
  //   ffff f07f 9*ffff
endmodule

module _16bit_compare (
  input  [15:0] A,
  input  [15:0] B,
  output [15:0] OUT
);

  wire comparator_1_eq, comparator_1_gt, comparator_1_lt;

  assign OUT = comparator_1_gt ? 16'h1 : 16'bz;  // Controlled_Buffer controlled_buffer_1
  assign OUT = comparator_1_eq ? {16{1'b0}} : 16'bz;  // Controlled_Buffer controlled_buffer_2
  assign OUT = comparator_1_lt ? {16{1'b1}} : 16'bz;  // Controlled_Buffer controlled_buffer_3
  Comparator #(.width(16)) comparator_1 (
    .a(A), .b(B), .gt(comparator_1_gt), .eq(comparator_1_eq), .lt(comparator_1_lt));
endmodule

module am08x24arc_decoder (
  input  [7:0] OPCODE,
  output STACK_PUSH,
  output STACK_POP,
  output STACK_SWAP,
  output SELECT_DEVICE,
  output DEVICE_ENABLE,
  output JZ,
  output JNEG,
  output JPOS,
  output PC,
  output [2:0] DATA_BUS_SRC,
  output [2:0] ADRESS_SRC,
  output [3:0] ALU_OP
);

  wire [23:19] rom_1_data;

  ROM #(.dataWidth(24), .Select("low")) rom_1 (
    .addr(OPCODE),
    .data({rom_1_data, STACK_PUSH, STACK_POP, STACK_SWAP, SELECT_DEVICE, DEVICE_ENABLE, JZ, JNEG, JPOS, PC, DATA_BUS_SRC, ADRESS_SRC, ALU_OP}));

  // Notes on the sheet:
  //   contents of rom_1 (hex, n*v repeats v):
  //   0 40000 40180 20000 40200 40280 10000 9*0 40100 40101 40102 40103 40104 40105 40106 40107 40108
  //   40109 400 19*0 8000
endmodule
